// Logisim project mips-like.circ as structural Verilog: 5 circuits, main circuit PROCESSADOR
module PROCESSADOR (
  output [31:0] \INSTRUÇÃO 
);

  wire button_1_out, clock_1_out, uc_control_1_escrever_reg, uc_control_1_jump;
  wire [3:0] uc_control_1_ula_op;
  wire [7:0] ram_1_data;
  wire [31:0] adder_1_out, banco_de_registradores_1_r0_d, banco_de_registradores_1_r1_d, PC_q;

  Adder #(.width(32)) adder_1 (.a(PC_q), .b(32'h4), .out(adder_1_out));  // open: cin, cout
  Register #(.width(32)) PC (.D(adder_1_out), .Q(PC_q), .clk(clock_1_out), .clr(button_1_out));  // open: en
  Clock clock_1 (.out(clock_1_out));
  Button button_1 (.out(button_1_out));
  ROM #(.dataWidth(32)) rom_1 (.addr(PC_q[9:2]), .data(\INSTRUÇÃO ));  // open: sel
  uc_control uc_control_1 (
    .E0(\INSTRUÇÃO [31]), .E1(\INSTRUÇÃO [30]), .E2(\INSTRUÇÃO [29]), .E3(\INSTRUÇÃO [28]),
    .ula_op(uc_control_1_ula_op), .escrever_reg(uc_control_1_escrever_reg), .jump(uc_control_1_jump));  // open: escrever_mem, branch, reg_mem, ler_mem
  BANCO_DE_REGISTRADORES banco_de_registradores_1 (
    .R0_D(banco_de_registradores_1_r0_d), .R1_D(banco_de_registradores_1_r1_d), .R0(\INSTRUÇÃO [19:16]),
    .R1(\INSTRUÇÃO [23:20]), .CLK(clock_1_out), .RW_2(\INSTRUÇÃO [27:24]), .RW(uc_control_1_escrever_reg),
    .RESET(button_1_out));  // open: DATA_WRITE
  ULA ula_1 (
    .DATA_0(banco_de_registradores_1_r0_d), .DATA_1(banco_de_registradores_1_r1_d),
    .ULA_OP(uc_control_1_ula_op));  // open: ULA_OUT, shamt
  RAM ram_1 (.data(ram_1_data));  // open: addr, sel, clk, ld, clr

  // Notes on the sheet:
  //   REG_0
  //   REG_1
  //   REG_W
  //   contents of rom_1 (hex, n*v repeats v):
  //   120000
  //   DATA_W
  //   REG0_D
  //   REG1_D
  //   ULA
endmodule

module ULA (
  input  [31:0] DATA_0,
  input  [31:0] DATA_1,
  input  [3:0] ULA_OP,
  input  [4:0] shamt,
  output [31:0] ULA_OUT
);

  wire comparator_1_eq, comparator_1_gt, comparator_1_lt;
  wire [31:0] adder_1_out, bit_extender_1_out, bit_extender_2_out, bit_extender_3_out, multiplier_1_out,
       shifter_1_out, shifter_2_out, subtractor_1_out;

  Adder #(.width(32)) adder_1 (.a(DATA_0), .b(DATA_1), .out(adder_1_out));  // open: cin, cout
  Subtractor #(.width(32)) subtractor_1 (.a(DATA_0), .b(DATA_1), .out(subtractor_1_out));  // open: bin, bout
  Multiplier #(.width(32)) multiplier_1 (.a(DATA_0), .b(DATA_1), .out(multiplier_1_out));  // open: cin, cout
  Comparator #(.width(32), .mode("unsigned")) comparator_1 (
    .a(DATA_0), .b(DATA_1), .gt(comparator_1_gt), .eq(comparator_1_eq), .lt(comparator_1_lt));
  Shifter #(.width(32)) shifter_1 (.in(DATA_0), .\dist (shamt), .out(shifter_1_out));
  Shifter #(.width(32), .shift("lr")) shifter_2 (.in(DATA_0), .\dist (shamt), .out(shifter_2_out));
  assign bit_extender_1_out = {{31{1'b0}}, comparator_1_gt};  // Bit_Extender bit_extender_1
  assign bit_extender_2_out = {{31{1'b0}}, comparator_1_eq};  // Bit_Extender bit_extender_2
  assign bit_extender_3_out = {{31{1'b0}}, comparator_1_lt};  // Bit_Extender bit_extender_3
  Multiplexer #(.select(4), .width(32)) multiplexer_1 (
    .in0(adder_1_out), .in1(subtractor_1_out), .in2(multiplier_1_out), .in3(bit_extender_1_out),
    .in4(bit_extender_2_out), .in5(bit_extender_3_out), .in6(shifter_1_out), .in7(shifter_2_out),
    .out(ULA_OUT), .sel(ULA_OP));  // open: in8, in9, in10, in11, in12, in13, in14, in15, en
endmodule

module UC (
  input  E0,
  input  E1,
  input  E2,
  input  E3,
  output ula_op,
  output write_reg
);

  wire and_1_out, and_2_out, not_1_out, not_2_out, not_3_out, not_4_out, not_5_out, not_6_out, not_7_out,
       not_8_out, not_9_out;

  not not_1 (not_1_out, E0);
  not not_2 (not_2_out, E1);
  not not_3 (not_3_out, E2);
  not not_4 (not_4_out, E0);
  and and_1 (and_1_out, not_4_out, not_5_out, not_6_out);
  not not_5 (not_5_out, E1);
  not not_6 (not_6_out, E2);
  not not_7 (not_7_out, E0);
  and and_2 (and_2_out, not_7_out, not_8_out, not_9_out);
  not not_8 (not_8_out, E1);
  not not_9 (not_9_out, E3);
  and and_3 (ula_op, not_1_out, not_2_out, not_3_out, E3);
  or or_1 (write_reg, and_1_out, and_2_out);
endmodule

module BANCO_DE_REGISTRADORES (
  input  [31:0] DATA_WRITE,
  input  CLK,
  input  RESET,
  input  RW,
  input  [3:0] R0,
  input  [3:0] RW_2,
  input  [3:0] R1,
  output [31:0] R0_D,
  output [31:0] R1_D
);

  wire _0000w, _0001w, _0010w, _0011w, _0100w, _0101w, _0110w, _0111w, _1000w, _1001w, _1010w, _1011w,
       _1100w, _1101w, _1110w, _1111w;
  wire [31:0] _0000, _0001, _0010, _0011, _0100, _0101, _0110, _0111, _1000, _1001, _1010, _1011, _1100,
       _1101, _1110, _1111;

  Multiplexer #(.select(4), .width(32), .disabled(0), .enable("false")) multiplexer_1 (
    .in0(_0000), .in1(_0001), .in2(_0010), .in3(_0011), .in4(_0100), .in5(_0101), .in6(_0110), .in7(_0111),
    .in8(_1000), .in9(_1001), .in10(_1010), .in11(_1011), .in12(_1100), .in13(_1101), .in14(_1110),
    .in15(_1111), .out(R0_D), .sel(R0));
  Multiplexer #(.select(4), .width(32), .disabled(0), .enable("false")) multiplexer_2 (
    .in0(_0000), .in1(_0001), .in2(_0010), .in3(_0011), .in4(_0100), .in5(_0101), .in6(_0110), .in7(_0111),
    .in8(_1000), .in9(_1001), .in10(_1010), .in11(_1011), .in12(_1100), .in13(_1101), .in14(_1110),
    .in15(_1111), .out(R1_D), .sel(R1));
  Register #(.width(32)) register_1 (.D(DATA_WRITE), .en(_0000w), .Q(_0000), .clk(CLK), .clr(RESET));
  Register #(.width(32)) register_2 (.D(DATA_WRITE), .en(_0001w), .Q(_0001), .clk(CLK), .clr(RESET));
  Register #(.width(32)) register_3 (.D(DATA_WRITE), .en(_0010w), .Q(_0010), .clk(CLK), .clr(RESET));
  Register #(.width(32)) register_4 (.D(DATA_WRITE), .en(_0011w), .Q(_0011), .clk(CLK), .clr(RESET));
  Register #(.width(32)) register_5 (.D(DATA_WRITE), .en(_0100w), .Q(_0100), .clk(CLK), .clr(RESET));
  Register #(.width(32)) register_6 (.D(DATA_WRITE), .en(_0101w), .Q(_0101), .clk(CLK), .clr(RESET));
  Register #(.width(32)) register_7 (.D(DATA_WRITE), .en(_0110w), .Q(_0110), .clk(CLK), .clr(RESET));
  Register #(.width(32)) register_8 (.D(DATA_WRITE), .en(_0111w), .Q(_0111), .clk(CLK), .clr(RESET));
  Register #(.width(32)) register_9 (.D(DATA_WRITE), .en(_1000w), .Q(_1000), .clk(CLK), .clr(RESET));
  Register #(.width(32)) register_10 (.D(DATA_WRITE), .en(_1001w), .Q(_1001), .clk(CLK), .clr(RESET));
  Register #(.width(32)) register_11 (.D(DATA_WRITE), .en(_1010w), .Q(_1010), .clk(CLK), .clr(RESET));
  Register #(.width(32)) register_12 (.D(DATA_WRITE), .en(_1011w), .Q(_1011), .clk(CLK), .clr(RESET));
  Demultiplexer #(.select(4)) demultiplexer_1 (
    .out0(_0000w), .out1(_0001w), .out2(_0010w), .out3(_0011w), .out4(_0100w), .out5(_0101w), .out6(_0110w),
    .out7(_0111w), .out8(_1000w), .out9(_1001w), .out10(_1010w), .out11(_1011w), .out12(_1100w),
    .out13(_1101w), .out14(_1110w), .out15(_1111w), .in(RW), .sel(RW_2));  // open: en
  Register #(.width(32)) register_13 (.D(DATA_WRITE), .en(_1100w), .Q(_1100), .clk(CLK), .clr(RESET));
  Register #(.width(32)) register_14 (.D(DATA_WRITE), .en(_1101w), .Q(_1101), .clk(CLK), .clr(RESET));
  Register #(.width(32)) register_15 (.D(DATA_WRITE), .en(_1110w), .Q(_1110), .clk(CLK), .clr(RESET));
  Register #(.width(32)) register_16 (.D(DATA_WRITE), .en(_1111w), .Q(_1111), .clk(CLK), .clr(RESET));

  // Other names for the same wires on the sheet: write_c[31:0] = DATA_WRITE
endmodule

module uc_control (
  input  E0,
  input  E1,
  input  E2,
  input  E3,
  output [3:0] ula_op,
  output escrever_reg,
  output escrever_mem,
  output jump,
  output branch,
  output reg_mem,
  output ler_mem
);

  wire and_1_out, and_2_out, and_3_out, and_4_out, not_1_out, not_2_out, not_3_out, not_4_out, not_5_out,
       not_6_out, not_7_out, not_8_out, not_9_out, not_10_out, not_11_out, not_12_out, not_13_out,
       not_14_out, not_15_out, not_16_out, not_17_out, not_18_out, not_19_out, not_20_out, not_21_out;

  not not_1 (not_1_out, E0);
  and and_1 (and_1_out, not_1_out, not_2_out);
  not not_2 (not_2_out, E1);
  not not_3 (not_3_out, E0);
  not not_4 (not_4_out, E2);
  and and_2 (and_2_out, not_3_out, not_4_out, not_5_out);
  not not_5 (not_5_out, E3);
  not not_6 (not_6_out, E1);
  not not_7 (not_7_out, E2);
  and and_3 (and_3_out, not_6_out, not_7_out, not_8_out);
  not not_8 (not_8_out, E3);
  not not_9 (not_9_out, E0);
  and and_4 (and_4_out, not_9_out, E2, E3);
  not not_10 (not_10_out, E1);
  not not_11 (not_11_out, E2);
  not not_12 (not_12_out, E3);
  not not_13 (not_13_out, E0);
  not not_14 (not_14_out, E2);
  not not_15 (not_15_out, E0);
  not not_16 (not_16_out, E3);
  not not_17 (not_17_out, E1);
  not not_18 (not_18_out, E2);
  not not_19 (not_19_out, E3);
  not not_20 (not_20_out, E1);
  not not_21 (not_21_out, E2);
  or or_1 (escrever_reg, and_1_out, and_2_out, and_3_out, and_4_out);
  and and_5 (escrever_mem, E0, not_10_out, not_11_out, not_12_out);
  and and_6 (jump, not_13_out, E1, not_14_out, E3);
  and and_7 (branch, not_15_out, E1, E2, not_16_out);
  and and_8 (reg_mem, E0, not_17_out, not_18_out, not_19_out);
  and and_9 (ler_mem, E0, not_20_out, not_21_out, E3);

  assign ula_op = {E3, E2, E1, E0};
endmodule
